# Fritzing sketch pantallav2 (saved by Fritzing 0.9.3b)

parts:
  U1 = ESP32S-HiLetgo [part_number=ESP32S-HiLetgo]
  OLED_I2C1 = OLED 128x64 I2C Monochrome Display
  U2 = LIPO-1000mAh [package=lipo-1000]

nets:
  N1: U1.GPIO11, U2.-
  N2: U1.VIN, U2.+
  N3: U1.GPIO6, OLED_I2C1.VDD
  N4: U1.GPIO7, OLED_I2C1.GND
  N5: U1.GPIO3, OLED_I2C1.SDA
  N6: U1.GPIO23, OLED_I2C1.SCK

custom parts:
  ESP32S-HiLetgo: HiLetgo ESP-WROOM-32 ESP32 ESP-32S Development Board 2.4GHz Dual-Mode WiFi + Bluetooth Dual Cores Microcontroller The ESP32 integrated with Antenna switches, RF Balun, power amplifiers, low-noise amplifiers, filters, and management modules, and the entire solution occupies the least area of PCB. 2.4 GHz Wi-Fi plus Bluetooth dual-mode chip, with TSMC Ultra-low power consumption 40nm technology,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
